# Fritzing sketch fritzing_diagram (saved by Fritzing 0.9.3b)
circuit board: 8.32234cm x 4.72367cm
breadboards: 1

parts:
  J1 = Camdenboss CTB0158-2 [part_number=CTB0158-2 package=THT]
  Q1 = MOSFET-NCHANNEL [part_number=30N06L package=to220v]
  U1 = ESP8266 NodeMCU LoLin module [part_number="NodeMCU V1.0"]
  Q2 = MOSFET-NCHANNEL [part_number=30N06L package=to220v]
  Q3 = MOSFET-NCHANNEL [part_number=30N06L package=to220v]
  Part1 = BME280 Breakout
  IC1 = Voltage Regulator [package=to220-adj]

nets:
  N1: J1.pin1, Q1.D, Q2.D, Q3.D, IC1.IN
  GND: J1.pin2, Q1.S, U1.GND, Q2.S, Q3.S, Part1.GND, IC1.ADJ
  N2: Q1.G, U1.D7
  N3: U1.D1, Part1.SCK/SCL
  N4: U1.D2, Part1.SDI/SDA
  3V3: U1.3V3, Part1.3.3V
  N5: U1.D5, Q3.G
  N6: U1.D6, Q2.G
  N7: U1.Vin, IC1.OUT

custom parts:
  ESP8266 NodeMCU LoLin module: ESP8266 based NodeMCU
